// Logisim project Exemplo_0504.circ as structural Verilog: 1 circuit, main circuit main
module main (
  input  in_1,
  input  in_2,
  output out_3,
  output out_4,
  output out_5,
  output out_6,
  output out_7
);

  wire nor_1_out, nor_2_out, nor_3_out, nor_4_out, nor_5_out, nor_6_out, nor_7_out, nor_8_out, nor_9_out,
       nor_10_out, nor_11_out, nor_12_out, nor_13_out, nor_14_out, nor_15_out;

  nor nor_1 (nor_1_out, 1'b0, 1'b0);
  nor nor_2 (nor_2_out, 1'b0, 1'b0);
  nor nor_3 (nor_3_out, 1'b0, 1'b0);
  nor nor_4 (nor_4_out, 1'b1, 1'b1);
  nor nor_5 (nor_5_out, 1'b1, 1'b1);
  nor nor_6 (nor_6_out, 1'b0, 1'b0);
  nor nor_7 (nor_7_out, 1'b1, 1'b1);
  nor nor_8 (nor_8_out, 1'b1, 1'b1);
  nor nor_9 (nor_9_out, in_1, in_1);
  nor nor_10 (nor_10_out, in_2, in_2);
  nor nor_11 (nor_11_out, nor_1_out, nor_2_out);
  nor nor_12 (nor_12_out, nor_3_out, nor_4_out);
  nor nor_13 (nor_13_out, nor_5_out, nor_6_out);
  nor nor_14 (nor_14_out, nor_7_out, nor_8_out);
  nor nor_15 (nor_15_out, nor_9_out, nor_10_out);
  nor nor_16 (out_3, nor_11_out, nor_11_out);
  nor nor_17 (out_4, nor_12_out, nor_12_out);
  nor nor_18 (out_5, nor_13_out, nor_13_out);
  nor nor_19 (out_6, nor_14_out, nor_14_out);
  nor nor_20 (out_7, nor_15_out, nor_15_out);

  // Notes on the sheet:
  //   ENTRADAS
  //   0
  //   0
  //   0
  //   1
  //   1
  //   0
  //   1
  //   1
  //   a'+b' usando NOR
endmodule
