// Logisim project Exemplo_0506.circ as structural Verilog: 1 circuit, main circuit main
module main (
  input  in_1,
  input  in_2,
  input  in_3,
  input  in_4,
  output out_5,
  output out_6,
  output out_7,
  output out_8,
  output out_9,
  output out_10
);

  wire nor_1_out, nor_2_out, nor_3_out, nor_4_out, nor_5_out, nor_6_out, nor_7_out, nor_8_out, nor_9_out,
       nor_10_out, nor_11_out, nor_12_out, nor_13_out, nor_14_out, nor_15_out, nor_16_out, nor_17_out,
       nor_18_out, nor_19_out, nor_20_out, nor_21_out, nor_22_out, nor_23_out, nor_24_out, nor_25_out,
       nor_26_out, nor_27_out, nor_28_out, nor_34_out, nor_35_out;

  nor nor_1 (nor_1_out, in_1, in_1);
  nor nor_2 (nor_2_out, in_2, in_2);
  nor nor_3 (nor_3_out, in_4, in_4);
  nor nor_4 (nor_4_out, in_3, in_3);
  nor nor_5 (nor_5_out, 1'b0, 1'b0);
  nor nor_6 (nor_6_out, 1'b0, 1'b0);
  nor nor_7 (nor_7_out, 1'b1, 1'b1);
  nor nor_8 (nor_8_out, 1'b0, 1'b0);
  nor nor_9 (nor_9_out, 1'b0, 1'b0);
  nor nor_10 (nor_10_out, 1'b1, 1'b1);
  nor nor_11 (nor_11_out, 1'b1, 1'b1);
  nor nor_12 (nor_12_out, 1'b1, 1'b1);
  nor nor_13 (nor_13_out, nor_1_out, nor_1_out);
  nor nor_14 (nor_14_out, in_2, in_2);
  nor nor_15 (nor_15_out, in_1, in_1);
  nor nor_16 (nor_16_out, nor_2_out, nor_2_out);
  nor nor_17 (nor_17_out, in_3, nor_3_out);
  nor nor_18 (nor_18_out, nor_4_out, in_4);
  nor nor_19 (nor_19_out, 1'b0, nor_5_out);
  nor nor_20 (nor_20_out, nor_6_out, 1'b0);
  nor nor_21 (nor_21_out, 1'b0, nor_7_out);
  nor nor_22 (nor_22_out, nor_8_out, 1'b1);
  nor nor_23 (nor_23_out, 1'b1, nor_9_out);
  nor nor_24 (nor_24_out, nor_10_out, 1'b0);
  nor nor_25 (nor_25_out, 1'b1, nor_11_out);
  nor nor_26 (nor_26_out, nor_12_out, 1'b1);
  nor nor_27 (nor_27_out, nor_13_out, nor_14_out);
  nor nor_28 (nor_28_out, nor_15_out, nor_16_out);
  nor nor_29 (out_10, nor_17_out, nor_18_out);
  nor nor_30 (out_5, nor_19_out, nor_20_out);
  nor nor_31 (out_6, nor_21_out, nor_22_out);
  nor nor_32 (out_7, nor_23_out, nor_24_out);
  nor nor_33 (out_8, nor_25_out, nor_26_out);
  nor nor_34 (nor_34_out, nor_27_out, nor_28_out);
  nor nor_35 (nor_35_out, nor_34_out, nor_34_out);
  nor nor_36 (out_9, nor_35_out, nor_35_out);

  // Notes on the sheet:
  //   ENTRADAS
  //   0
  //   0
  //   0
  //   1
  //   1
  //   0
  //   1
  //   1
  //   (a^b)' usando NOR
  //   OU
endmodule
