// Logisim project Exemplo_0507.circ as structural Verilog: 1 circuit, main circuit main
module main (
  input  in_1,
  input  in_2,
  input  in_3,
  input  in_4,
  output out_5,
  output out_6,
  output out_7,
  output out_8,
  output out_9,
  output out_10
);

  wire nand_1_out, nand_2_out, nand_3_out, nand_4_out, nand_5_out, nand_6_out, nand_7_out, nand_8_out,
       nand_9_out, nand_10_out, nand_11_out, nand_12_out, nand_13_out, nand_14_out, nand_15_out, nand_16_out,
       nand_17_out, nand_18_out, nand_19_out, nand_20_out, nand_21_out, nand_22_out, nand_23_out,
       nand_24_out, nand_29_out, nand_30_out, nand_32_out, nand_33_out;

  nand nand_1 (nand_1_out, 1'b0, 1'b0);
  nand nand_2 (nand_2_out, 1'b0, 1'b0);
  nand nand_3 (nand_3_out, 1'b0, 1'b0);
  nand nand_4 (nand_4_out, 1'b1, 1'b1);
  nand nand_5 (nand_5_out, 1'b1, 1'b1);
  nand nand_6 (nand_6_out, 1'b0, 1'b0);
  nand nand_7 (nand_7_out, 1'b1, 1'b1);
  nand nand_8 (nand_8_out, 1'b1, 1'b1);
  nand nand_9 (nand_9_out, in_1, in_1);
  nand nand_10 (nand_10_out, in_2, in_2);
  nand nand_11 (nand_11_out, in_3, in_3);
  nand nand_12 (nand_12_out, in_4, in_4);
  nand nand_13 (nand_13_out, nand_1_out, 1'b0);
  nand nand_14 (nand_14_out, 1'b0, nand_2_out);
  nand nand_15 (nand_15_out, nand_3_out, 1'b1);
  nand nand_16 (nand_16_out, 1'b0, nand_4_out);
  nand nand_17 (nand_17_out, nand_5_out, 1'b0);
  nand nand_18 (nand_18_out, 1'b1, nand_6_out);
  nand nand_19 (nand_19_out, nand_7_out, 1'b1);
  nand nand_20 (nand_20_out, 1'b1, nand_8_out);
  nand nand_21 (nand_21_out, nand_9_out, in_2);
  nand nand_22 (nand_22_out, in_1, nand_10_out);
  nand nand_23 (nand_23_out, nand_11_out, in_4);
  nand nand_24 (nand_24_out, in_3, nand_12_out);
  nand nand_25 (out_5, nand_13_out, nand_14_out);
  nand nand_26 (out_6, nand_15_out, nand_16_out);
  nand nand_27 (out_7, nand_17_out, nand_18_out);
  nand nand_28 (out_8, nand_19_out, nand_20_out);
  nand nand_29 (nand_29_out, nand_21_out, nand_21_out);
  nand nand_30 (nand_30_out, nand_22_out, nand_22_out);
  nand nand_31 (out_10, nand_23_out, nand_24_out);
  nand nand_32 (nand_32_out, nand_29_out, nand_29_out);
  nand nand_33 (nand_33_out, nand_30_out, nand_30_out);
  nand nand_34 (out_9, nand_32_out, nand_33_out);

  // Notes on the sheet:
  //   ENTRADAS
  //   0
  //   0
  //   0
  //   1
  //   1
  //   0
  //   1
  //   1
  //   (a^b) usando NAND
  //   OU
endmodule
