// Logisim project Guia06_1.circ as structural Verilog: 1 circuit, main circuit main
module main (
  input  X,
  input  Y,
  input  Z,
  input  X_2,
  input  Y_2,
  input  Z_2,
  input  X_3,
  input  Y_3,
  input  Z_3,
  input  X_4,
  input  Y_4,
  input  Z_4,
  input  X_5,
  input  Y_5,
  input  Z_5,
  output out_16,
  output out_17,
  output out_18,
  output out_19,
  output out_20,
  output out_21,
  output out_22,
  output out_23,
  output out_24,
  output out_25
);

  wire and_1_out, and_2_out, and_3_out, and_4_out, and_5_out, and_6_out, and_7_out, and_8_out, and_9_out,
       and_10_out, and_11_out, and_12_out, and_13_out, and_14_out, and_15_out, and_16_out, and_17_out,
       and_18_out, and_19_out, and_20_out, and_21_out, and_22_out, and_23_out, and_24_out, and_25_out,
       and_26_out, and_27_out, and_28_out, and_29_out, and_30_out, not_1_out, not_2_out, not_3_out,
       not_4_out, not_5_out, not_6_out, not_7_out, not_8_out, not_9_out, not_10_out, not_11_out, not_12_out,
       not_13_out, not_14_out, not_15_out;

  not not_1 (not_1_out, X_2);
  not not_2 (not_2_out, Z_2);
  not not_3 (not_3_out, Y_2);
  not not_4 (not_4_out, Y_3);
  not not_5 (not_5_out, X_3);
  not not_6 (not_6_out, X_5);
  not not_7 (not_7_out, Y_5);
  not not_8 (not_8_out, Z_3);
  not not_9 (not_9_out, Z_5);
  and and_1 (and_1_out, Y_2, Z_2);
  or or_1 (out_16, and_1_out, and_2_out);
  and and_2 (and_2_out, X_2, Z_2);
  and and_3 (and_3_out, not_1_out, Y_2, Z_2);
  and and_4 (and_4_out, X_2, Y_2, Z_2);
  or or_2 (out_18, and_3_out, and_4_out, and_5_out);
  and and_5 (and_5_out, X_2, not_3_out, Z_2);
  and and_6 (and_6_out, X_3, not_8_out);
  or or_3 (out_20, and_6_out, and_7_out);
  and and_7 (and_7_out, Y_3, not_8_out);
  and and_8 (and_8_out, not_5_out, Y_3, not_8_out);
  and and_9 (and_9_out, X_3, Y_3, not_8_out);
  and and_10 (and_10_out, X_3, not_4_out, not_8_out);
  and and_11 (and_11_out, Y_5, not_9_out);
  or or_4 (out_24, and_11_out, and_12_out, and_13_out);
  and and_12 (and_12_out, X_5, not_9_out);
  and and_13 (and_13_out, X_5, Y_5);
  and and_14 (and_14_out, not_6_out, Y_5, not_9_out);
  and and_15 (and_15_out, X_5, Y_5, not_9_out);
  and and_16 (and_16_out, X_5, not_7_out, not_9_out);
  and and_17 (and_17_out, X_5, Y_5, Z_5);
  or or_5 (out_22, and_8_out, and_9_out, and_10_out);
  or or_6 (out_25, and_14_out, and_15_out, and_16_out, and_17_out);
  not not_10 (not_10_out, Y);
  not not_11 (not_11_out, X);
  not not_12 (not_12_out, Y_4);
  not not_13 (not_13_out, X_4);
  not not_14 (not_14_out, Z);
  not not_15 (not_15_out, Z_4);
  and and_18 (and_18_out, not_11_out, Z);
  and and_19 (and_19_out, not_10_out, Z);
  and and_20 (and_20_out, not_11_out, Y);
  and and_21 (and_21_out, not_11_out, Y, not_14_out);
  and and_22 (and_22_out, not_11_out, not_10_out, Z);
  and and_23 (and_23_out, not_11_out, Y, Z);
  and and_24 (and_24_out, X, not_10_out, Z);
  and and_25 (and_25_out, not_13_out, not_15_out);
  and and_26 (and_26_out, X_4, Z_4);
  and and_27 (and_27_out, not_13_out, not_12_out, not_15_out);
  and and_28 (and_28_out, not_13_out, Y_4, not_15_out);
  and and_29 (and_29_out, X_4, Y_4, Z_4);
  and and_30 (and_30_out, X_4, not_12_out, Z_4);
  or or_7 (out_17, and_18_out, and_19_out, and_20_out);
  or or_8 (out_19, and_21_out, and_22_out, and_23_out, and_24_out);
  or or_9 (out_21, and_25_out, and_26_out);
  or or_10 (out_23, and_27_out, and_28_out, and_29_out, and_30_out);

  // Notes on the sheet:
  //   LETRA A
  //   LETRA B
  //   LETRA C
  //   LETRA D
endmodule
