// Logisim project Guia06_3.circ as structural Verilog: 1 circuit, main circuit main
module main (
  input  w,
  input  X,
  input  Y,
  input  Z,
  input  w_2,
  input  X_2,
  input  Y_2,
  input  Z_2,
  input  w_3,
  input  X_3,
  input  Y_3,
  input  Z_3,
  input  w_4,
  input  X_4,
  input  Y_4,
  input  Z_4,
  input  w_5,
  input  X_5,
  input  Y_5,
  input  Z_5,
  output out_21,
  output out_22,
  output out_23,
  output out_24,
  output out_25,
  output out_26,
  output out_27,
  output out_28,
  output out_29,
  output out_30
);

  wire and_1_out, and_2_out, and_3_out, and_4_out, and_5_out, and_6_out, and_7_out, and_8_out, and_9_out,
       and_10_out, and_11_out, and_12_out, and_13_out, and_14_out, and_15_out, and_16_out, and_17_out,
       and_18_out, and_19_out, and_20_out, and_21_out, and_22_out, and_23_out, and_24_out, and_25_out,
       and_26_out, and_27_out, and_28_out, and_29_out, and_30_out, and_31_out, and_32_out, and_33_out,
       and_34_out, and_35_out, and_36_out, and_37_out, and_38_out, and_39_out, and_40_out, and_41_out,
       and_42_out, and_43_out, and_44_out, and_45_out, and_46_out, and_47_out, and_48_out, and_49_out,
       and_50_out, and_51_out, and_52_out, and_53_out, and_54_out, and_55_out, and_56_out, and_57_out,
       not_1_out, not_2_out, not_3_out, not_4_out, not_5_out, not_6_out, not_7_out, not_8_out, not_9_out,
       not_10_out, not_11_out, not_12_out, not_13_out, not_14_out, not_15_out, not_16_out, not_17_out,
       not_18_out, not_19_out, not_20_out;

  not not_1 (not_1_out, w_2);
  not not_2 (not_2_out, Z_2);
  not not_3 (not_3_out, X_2);
  not not_4 (not_4_out, Y_2);
  and and_1 (and_1_out, not_3_out, not_4_out, Z_2);
  or or_1 (out_21, and_1_out, and_2_out, and_3_out);
  and and_2 (and_2_out, not_3_out, Y_2, w_2);
  and and_3 (and_3_out, X_2, not_4_out, w_2);
  and and_4 (and_4_out, not_1_out, not_3_out, not_4_out, Z_2);
  and and_5 (and_5_out, w_2, not_3_out, not_4_out, Z_2);
  and and_6 (and_6_out, w_2, not_3_out, Y_2, Z_2);
  and and_7 (and_7_out, w_2, not_3_out, Y_2, not_2_out);
  and and_8 (and_8_out, w_2, X_2, not_4_out, Z_2);
  and and_9 (and_9_out, w_2, X_2, not_4_out, not_2_out);
  or or_2 (out_26, and_4_out, and_5_out, and_6_out, and_7_out, and_8_out, and_9_out);
  not not_5 (not_5_out, w_3);
  not not_6 (not_6_out, X_3);
  not not_7 (not_7_out, Z_3);
  not not_8 (not_8_out, Y_3);
  and and_10 (and_10_out, not_6_out, not_8_out, not_5_out);
  and and_11 (and_11_out, not_6_out, not_8_out, not_7_out);
  and and_12 (and_12_out, Y_3, not_5_out, Z_3);
  and and_13 (and_13_out, X_3, Y_3, not_5_out);
  and and_14 (and_14_out, not_5_out, not_6_out, not_8_out, not_7_out);
  and and_15 (and_15_out, w_3, not_6_out, not_8_out, Z_3);
  and and_16 (and_16_out, w_3, not_6_out, not_8_out, not_7_out);
  and and_17 (and_17_out, not_5_out, not_6_out, Y_3, Z_3);
  and and_18 (and_18_out, not_5_out, X_3, Y_3, not_7_out);
  and and_19 (and_19_out, not_5_out, X_3, not_8_out, not_7_out);
  and and_20 (and_20_out, not_5_out, X_3, not_8_out, Z_3);
  or or_3 (out_22, and_10_out, and_11_out, and_12_out, and_13_out);
  or or_4 (out_27, and_14_out, and_15_out, and_16_out, and_17_out, and_18_out, and_19_out, and_20_out);
  not not_9 (not_9_out, w_5);
  not not_10 (not_10_out, X_5);
  not not_11 (not_11_out, Y_5);
  not not_12 (not_12_out, Z_5);
  and and_21 (and_21_out, not_10_out, w_5, not_12_out);
  and and_22 (and_22_out, not_10_out, not_11_out, not_9_out);
  and and_23 (and_23_out, not_11_out, not_9_out, not_12_out);
  and and_24 (and_24_out, not_10_out, not_9_out, not_12_out);
  and and_25 (and_25_out, X_5, w_5, Z_5);
  and and_26 (and_26_out, not_9_out, not_10_out, not_11_out, not_12_out);
  and and_27 (and_27_out, not_9_out, not_10_out, not_11_out, Z_5);
  and and_28 (and_28_out, w_5, not_10_out, not_11_out, not_12_out);
  and and_29 (and_29_out, not_9_out, not_10_out, Y_5, not_12_out);
  and and_30 (and_30_out, w_5, not_10_out, Y_5, not_12_out);
  and and_31 (and_31_out, w_5, X_5, Y_5, Z_5);
  and and_32 (and_32_out, not_9_out, X_5, not_11_out, not_12_out);
  and and_33 (and_33_out, w_5, X_5, not_11_out, Z_5);
  or or_5 (out_25, and_21_out, and_22_out, and_23_out, and_24_out, and_25_out);
  or or_6 (out_30, and_26_out, and_27_out, and_28_out, and_29_out, and_30_out, and_31_out, and_32_out, and_33_out);
  not not_13 (not_13_out, w_4);
  not not_14 (not_14_out, Z_4);
  not not_15 (not_15_out, Y_4);
  not not_16 (not_16_out, X_4);
  and and_34 (and_34_out, not_15_out, w_4, not_14_out);
  and and_35 (and_35_out, X_4, w_4, not_14_out);
  and and_36 (and_36_out, X_4, not_15_out, w_4);
  and and_37 (and_37_out, not_16_out, Y_4, not_13_out);
  and and_38 (and_38_out, not_16_out, Y_4, Z_4);
  and and_39 (and_39_out, w_4, not_16_out, not_15_out, not_14_out);
  and and_40 (and_40_out, not_13_out, not_16_out, Y_4, not_14_out);
  and and_41 (and_41_out, not_13_out, not_16_out, Y_4, Z_4);
  and and_42 (and_42_out, w_4, not_16_out, Y_4, Z_4);
  and and_43 (and_43_out, w_4, X_4, Y_4, not_14_out);
  and and_44 (and_44_out, w_4, X_4, not_15_out, Z_4);
  and and_45 (and_45_out, w_4, X_4, not_15_out, not_14_out);
  or or_7 (out_24, and_34_out, and_35_out, and_36_out, and_37_out, and_38_out);
  or or_8 (out_28, and_39_out, and_40_out, and_41_out, and_42_out, and_43_out, and_44_out, and_45_out);
  not not_17 (not_17_out, X);
  not not_18 (not_18_out, w);
  not not_19 (not_19_out, Z);
  not not_20 (not_20_out, Y);
  and and_46 (and_46_out, not_17_out, not_20_out, not_18_out);
  and and_47 (and_47_out, not_17_out, w, not_19_out);
  and and_48 (and_48_out, X, Y, w);
  and and_49 (and_49_out, X, not_20_out, not_18_out);
  and and_50 (and_50_out, not_18_out, not_17_out, not_20_out, not_19_out);
  and and_51 (and_51_out, not_18_out, not_17_out, not_20_out, Z);
  and and_52 (and_52_out, w, not_17_out, not_20_out, not_19_out);
  and and_53 (and_53_out, w, not_17_out, Y, not_19_out);
  and and_54 (and_54_out, w, X, Y, Z);
  and and_55 (and_55_out, w, X, Y, not_19_out);
  and and_56 (and_56_out, not_18_out, X, not_20_out, not_19_out);
  and and_57 (and_57_out, not_18_out, X, not_20_out, Z);
  or or_9 (out_23, and_46_out, and_47_out, and_48_out, and_49_out);
  or or_10 (out_29, and_50_out, and_51_out, and_52_out, and_53_out, and_54_out, and_55_out, and_56_out, and_57_out);

  // Notes on the sheet:
  //   LETRA A
  //   LETRA B
  //   LETRA C
  //   LETRA D
  //   LETRA E
endmodule
