// Logisim project Exemplo_0801.circ as structural Verilog: 3 circuits, main circuit main
module main (
  input  a3,
  input  in_2,
  input  in_3,
  input  a0,
  input  b3,
  input  in_6,
  input  in_7,
  input  b0,
  output s4,
  output s3,
  output s2,
  output s1,
  output s0
);

  wire fulladd_1_vai_um, fulladd_2_vai_um, fulladd_3_vai_um;

  FullADD fulladd_1 (.v(1'b0), .x(a0), .y(b0), .soma(s0), .vai_um(fulladd_1_vai_um));
  FullADD fulladd_2 (.v(fulladd_1_vai_um), .x(in_3), .y(in_7), .soma(s1), .vai_um(fulladd_2_vai_um));
  FullADD fulladd_3 (.v(fulladd_2_vai_um), .x(in_2), .y(in_6), .soma(s2), .vai_um(fulladd_3_vai_um));
  FullADD fulladd_4 (.v(fulladd_3_vai_um), .x(a3), .y(b3), .soma(s3), .vai_um(s4));

  // Notes on the sheet:
  //   Soma (3+1 = 4) ou (11+01=100)
endmodule

module FullADD (
  input  v,
  input  x,
  input  y,
  output soma,
  output vai_um
);

  wire halfadd_1_soma, halfadd_1_vai_um, halfadd_2_vai_um;

  HalfADD halfadd_1 (.x(x), .y(y), .soma(halfadd_1_soma), .vai_um(halfadd_1_vai_um));
  HalfADD halfadd_2 (.x(v), .y(halfadd_1_soma), .soma(soma), .vai_um(halfadd_2_vai_um));
  or or_1 (vai_um, halfadd_2_vai_um, halfadd_1_vai_um);
endmodule

module HalfADD (
  input  x,
  input  y,
  output soma,
  output vai_um
);

  xor xor_1 (soma, x, y);
  and and_1 (vai_um, y, x);
endmodule
