// Logisim project Exemplo_0802.circ as structural Verilog: 3 circuits, main circuit main
module main (
  input  a4,
  input  in_2,
  input  in_3,
  input  in_4,
  input  a0,
  input  b4,
  input  in_7,
  input  in_8,
  input  in_9,
  input  b0,
  output s5,
  output s4,
  output s3,
  output s2,
  output s1,
  output s0
);

  wire fulldif_1_vai_um, fulldif_2_vai_um, fulldif_3_vai_um, fulldif_4_vai_um;

  FullDIF fulldif_1 (.v(1'b0), .x(a0), .y(b0), .diff(s0), .vai_um(fulldif_1_vai_um));
  FullDIF fulldif_2 (.v(fulldif_1_vai_um), .x(in_4), .y(in_9), .diff(s1), .vai_um(fulldif_2_vai_um));
  FullDIF fulldif_3 (.v(fulldif_2_vai_um), .x(in_3), .y(in_8), .diff(s2), .vai_um(fulldif_3_vai_um));
  FullDIF fulldif_4 (.v(fulldif_3_vai_um), .x(in_2), .y(in_7), .diff(s3), .vai_um(fulldif_4_vai_um));
  FullDIF fulldif_5 (.v(fulldif_4_vai_um), .x(a4), .y(b4), .diff(s4), .vai_um(s5));

  // Notes on the sheet:
  //   Diferenca (3-1 = 2) ou (11-01=10)
endmodule

module HalfDIF (
  input  x,
  input  y,
  output diff,
  output vai_um
);

  wire not_1_out;

  not not_1 (not_1_out, x);
  xor xor_1 (diff, x, y);
  and and_1 (vai_um, y, not_1_out);
endmodule

module FullDIF (
  input  v,
  input  x,
  input  y,
  output diff,
  output vai_um
);

  wire halfdif_1_vai_um, halfdif_2_diff, halfdif_2_vai_um;

  HalfDIF halfdif_1 (.x(halfdif_2_diff), .y(v), .diff(diff), .vai_um(halfdif_1_vai_um));
  HalfDIF halfdif_2 (.x(x), .y(y), .diff(halfdif_2_diff), .vai_um(halfdif_2_vai_um));
  or or_1 (vai_um, halfdif_1_vai_um, halfdif_2_vai_um);
endmodule
