// Logisim project Exemplo_0804.circ as structural Verilog: 2 circuits, main circuit main
module main (
  input  a4,
  input  in_2,
  input  in_3,
  input  in_4,
  input  a0,
  input  b4,
  input  in_7,
  input  in_8,
  input  in_9,
  input  b0,
  output s0
);

  compXOR compxor_1 (
    .a0(a0), .b0(b0), .a1(in_4), .b1(in_9), .a2(in_3), .b2(in_8), .a3(in_2), .b3(in_7), .a4(a4), .b4(b4),
    .out_11(s0));

  // Notes on the sheet:
  //   se a saida for 0 os numeros são iguais
endmodule

module compXOR (
  input  a0,
  input  b0,
  input  a1,
  input  b1,
  input  a2,
  input  b2,
  input  a3,
  input  b3,
  input  a4,
  input  b4,
  output out_11
);

  wire xor_1_out, xor_2_out, xor_3_out, xor_4_out, xor_5_out;

  xor xor_1 (xor_1_out, a0, b0);
  xor xor_2 (xor_2_out, a1, b1);
  xor xor_3 (xor_3_out, a2, b2);
  xor xor_4 (xor_4_out, a3, b3);
  xor xor_5 (xor_5_out, a4, b4);
  or or_1 (out_11, xor_1_out, xor_2_out, xor_3_out, xor_4_out, xor_5_out);
endmodule
