// Logisim project Exemplo_0805.circ as structural Verilog: 3 circuits, main circuit main
module main (
  input  a5,
  input  in_2,
  input  in_3,
  input  in_4,
  input  in_5,
  input  a0,
  output s5,
  output s4,
  output s3,
  output s2,
  output s1,
  output s0
);

  Complemento2 complemento2_1 (
    .a0(a0), .in_2(in_5), .in_3(in_4), .in_4(in_3), .in_5(in_2), .a5(a5), .s0(s0), .s1(s1), .s2(s2), .s3(s3),
    .s4(s4), .s5(s5));
endmodule

module Complemento2 (
  input  a0,
  input  in_2,
  input  in_3,
  input  in_4,
  input  in_5,
  input  a5,
  output s0,
  output s1,
  output s2,
  output s3,
  output s4,
  output s5
);

  wire add_1_out_4, add_2_out_4, add_3_out_4, add_4_out_4, add_5_out_4, not_1_out, not_2_out, not_3_out,
       not_4_out, not_5_out, not_6_out;

  not not_1 (not_1_out, a0);
  not not_2 (not_2_out, in_2);
  not not_3 (not_3_out, in_3);
  not not_4 (not_4_out, in_4);
  not not_5 (not_5_out, in_5);
  not not_6 (not_6_out, a5);
  ADD add_1 (.x(1'b1), .v(not_1_out), .out_3(s0), .out_4(add_1_out_4));
  ADD add_2 (.x(add_1_out_4), .v(not_2_out), .out_3(s1), .out_4(add_2_out_4));
  ADD add_3 (.x(add_2_out_4), .v(not_3_out), .out_3(s2), .out_4(add_3_out_4));
  ADD add_4 (.x(add_3_out_4), .v(not_4_out), .out_3(s3), .out_4(add_4_out_4));
  ADD add_5 (.x(add_4_out_4), .v(not_5_out), .out_3(s4), .out_4(add_5_out_4));
  ADD add_6 (.x(add_5_out_4), .v(not_6_out), .out_3(s5));  // open: out_4
endmodule

module ADD (
  input  x,
  input  v,
  output out_3,
  output out_4
);

  xor xor_1 (out_3, x, v);
  and and_1 (out_4, x, v);
endmodule
